// Logisim project B-Bus.circ as structural Verilog
module B_Bus (
  input  [31:0] in_1,
  input  [31:0] in_2,
  input  [31:0] in_3,
  input  [31:0] in_4,
  input  [31:0] in_5,
  input  [31:0] in_6,
  input  [31:0] in_7,
  input  [31:0] in_8,
  input  [31:0] in_9,
  output [31:0] out_10
);

  assign out_10 = in_9 | in_8 | in_7 | in_6 | in_5 | in_4 | in_3 | in_2 | in_1;  // OR_Gate or_1, 32 bits wide
endmodule
