// Logisim project CSC3410-MicroArchitecture.circ as structural Verilog: 34 circuits, main circuit Addr
// MDR
module main (
);

  wire alu_1_n_flag, alu_1_z_flag, decoder_1_out_2, decoder_1_out_3, decoder_1_out_4, decoder_1_out_5,
       decoder_1_out_6, decoder_1_out_7, decoder_1_out_8, decoder_1_out_9, decoder_1_out_10, Halt,
       high_bit_1_out_5, mi_display_1_out_5, mi_display_1_out_6, mi_display_1_out_7, mir_1_out_2,
       mir_1_out_8, mir_1_out_9, mir_1_out_10, mir_1_out_11, mir_1_out_12, mir_1_out_13, mir_1_out_14,
       mir_1_out_15, mir_1_out_16, t1, t2, t3, t4;
  wire [1:0] mir_1_out_5, mir_1_out_6;
  wire [2:0] mir_1_out_3;
  wire [3:0] b_1_out_2, control_store_1_out_3, mi_display_1_out_2, mi_display_1_out_3, mi_display_1_out_4;
  wire [5:0] mir_1_out_7;
  wire [7:0] mbr_1_to_juntion_box, MBR_Probe, ram_1_mbr;
  wire [8:0] Micro_Instruction, mir_1_out_4, o_1_out_4;
  wire [31:0] alu_1_out_5, control_store_1_out_2, CPP_Probe, h_1_a_bus, H_Probe, LV_Probe,
       mar_1_output_to_ram, MAR_Probe, mbr_1_signed_output_2, mdr_1_output_to_ram, MDR_Probe, OPC_Probe,
       pc_1_ram_output, PC_Probe, ram_1_mdr_2, shifter_1_out_3, SP_Probe, TOS_Probe;

  Hex_Digit_Display hex_digit_display_1 (.value(mi_display_1_out_2), .dp(mi_display_1_out_5));
  // Probe on MAR_Probe
  // Probe on MDR_Probe
  // Probe on PC_Probe
  // Probe on MBR_Probe
  // Probe on SP_Probe
  // Probe on LV_Probe
  // Probe on CPP_Probe
  // Probe on TOS_Probe
  // Probe on OPC_Probe
  // Probe on H_Probe
  MI_Display mi_display_1 (
    .Microinstruction(Micro_Instruction), .out_2(mi_display_1_out_2), .out_3(mi_display_1_out_3),
    .out_4(mi_display_1_out_4), .out_5(mi_display_1_out_5), .out_7(mi_display_1_out_7),
    .out_6(mi_display_1_out_6));
  Hex_Digit_Display hex_digit_display_2 (.value(mi_display_1_out_3), .dp(mi_display_1_out_7));
  Hex_Digit_Display hex_digit_display_3 (.value(mi_display_1_out_4), .dp(mi_display_1_out_6));
  // Probe on mir_1_out_3
  RAM ram_1 (
    .MAR(mar_1_output_to_ram), .PC(pc_1_ram_output), .MDR_2(ram_1_mdr_2), .MDR(mdr_1_output_to_ram),
    .MBR(ram_1_mbr), .WRF(mir_1_out_3), .rw_clock(t3), .f_clock(t4));
  Master_Clock master_clock_1 (.Out_0(t1), .Out_1(t2), .Out_2(t3), .Out_3(t4), .Halt(Halt));
  // Probe on ram_1_mbr
  MBR mbr_1 (
    .RAM_Input(ram_1_mbr), .Signed_Output(decoder_1_out_5), .Signed_Output_2(mbr_1_signed_output_2),
    .Unsigned_Output_2(mbr_1_signed_output_2), .Unsigned_Output(decoder_1_out_4),
    .To_Juntion_Box(mbr_1_to_juntion_box), .Probe_Output(MBR_Probe), .WRF(mir_1_out_3), .Clock(t2));
  SP sp_1 (
    .C_Bus(shifter_1_out_3), .Clock(t2), .Enable_C_Bus(mir_1_out_13), .B_Bus(mbr_1_signed_output_2),
    .Enable_B_Bus(decoder_1_out_6), .Probe(SP_Probe));
  LV lv_1 (
    .C_Bus(shifter_1_out_3), .Clock(t2), .C_Bus_Enabled(mir_1_out_12), .B_Bus(mbr_1_signed_output_2),
    .Enable_B_Bus(decoder_1_out_7), .Probe(LV_Probe));
  CPP cpp_1 (
    .in_1(shifter_1_out_3), .Clock(t2), .Enabled(mir_1_out_11), .out_6(mbr_1_signed_output_2),
    .Enable_Output(decoder_1_out_8), .Probe(CPP_Probe));
  TOS tos_1 (
    .in_1(shifter_1_out_3), .Clock(t2), .Enabled(mir_1_out_10), .out_6(mbr_1_signed_output_2),
    .Enable_Output(decoder_1_out_9), .Probe(TOS_Probe));
  OPC opc_1 (
    .in_1(shifter_1_out_3), .Clock(t2), .Enabled(mir_1_out_9), .out_6(mbr_1_signed_output_2),
    .Enable_Output(decoder_1_out_10), .Probe(OPC_Probe));
  H h_1 (.C_Bus(shifter_1_out_3), .Clock(t2), .Enable_C_Bus(mir_1_out_8), .A_Bus(h_1_a_bus), .Probe(H_Probe));
  ALU alu_1 (
    .Z_Flag(alu_1_z_flag), .in_1(h_1_a_bus), .in_2(mbr_1_signed_output_2), .out_5(alu_1_out_5),
    .in_3(mir_1_out_7), .N_Flag(alu_1_n_flag));  // open: Carry_Out
  MAR mar_1 (
    .Input_from_C_Bus(shifter_1_out_3), .Clock(t2), .Enable_C_Bus(mir_1_out_16),
    .Output_to_RAM(mar_1_output_to_ram), .Probe_Output(MAR_Probe));
  MDR mdr_1 (
    .C_Bus_Input(shifter_1_out_3), .Clock(t2), .C_Bus_Enabled(mir_1_out_15),
    .B_Bus_Output(mbr_1_signed_output_2), .Enable_B_Bus(decoder_1_out_2), .Input_from_RAM(ram_1_mdr_2),
    .Output_to_RAM(mdr_1_output_to_ram), .WRF(mir_1_out_3), .Probe_Output(MDR_Probe));
  PC pc_1 (
    .C_Bus_Input(shifter_1_out_3), .Clock(t2), .B_Bus_Output(mbr_1_signed_output_2),
    .Enable_B_Bus(decoder_1_out_3), .Enable_C_Bus(mir_1_out_14), .RAM_Output(pc_1_ram_output),
    .Probe_Output(PC_Probe));
  Shifter shifter_1 (.in_1(alu_1_out_5), .out_3(shifter_1_out_3), .Controls(mir_1_out_6));
  Pull_Resistor pull_resistor_1 (.node(mbr_1_signed_output_2));
  Decoder decoder_1 (
    .in_1(b_1_out_2), .out_2(decoder_1_out_2), .out_3(decoder_1_out_3), .out_4(decoder_1_out_4),
    .out_5(decoder_1_out_5), .out_6(decoder_1_out_6), .out_7(decoder_1_out_7), .out_8(decoder_1_out_8),
    .out_9(decoder_1_out_9), .out_10(decoder_1_out_10));
  High_Bit high_bit_1 (
    .N(alu_1_n_flag), .out_5(high_bit_1_out_5), .in_2(t2), .JAMN_JAMZ(mir_1_out_5), .Z(alu_1_z_flag));
  MPC mpc_1 (.out_4(Micro_Instruction), .in_2(high_bit_1_out_5), .in_1(o_1_out_4), .in_3(t1));
  O o_1 (.ADDR(mir_1_out_4), .out_4(o_1_out_4), .MBR(mbr_1_to_juntion_box), .JMPC(mir_1_out_2));
  MIR mir_1 (
    .in_1(control_store_1_out_2), .out_4(mir_1_out_4), .out_5(mir_1_out_5), .out_6(mir_1_out_6),
    .out_7(mir_1_out_7), .out_8(mir_1_out_8), .out_9(mir_1_out_9), .out_10(mir_1_out_10),
    .out_11(mir_1_out_11), .out_3(mir_1_out_3), .out_12(mir_1_out_12), .out_13(mir_1_out_13),
    .out_14(mir_1_out_14), .out_15(mir_1_out_15), .out_16(mir_1_out_16), .out_2(mir_1_out_2));
  Control_Store control_store_1 (
    .out_2(control_store_1_out_2), .out_3(control_store_1_out_3), .in_1(Micro_Instruction), .Halt(Halt));
  B b_1 (.in_1(control_store_1_out_3), .out_2(b_1_out_2));

  // Notes on the sheet:
  //   10/20/15
  //   Nick Zayatz
  //   Michele Burns
  //   Michael Newton
  //   Charlie Adams
  //   Main File for CSC3410-MicroArchitecture Project
  //   JAMN/JAMZ
endmodule

module Addr (
  input  [8:0] in_1,
  output [8:0] out_2
);


  assign out_2 = in_1;

  // Notes on the sheet:
  //   in_1: pull=down
endmodule

module ALU (
  input  [31:0] in_1,
  input  [31:0] in_2,
  input  [5:0] in_3,
  output Z_Flag,
  output [31:0] out_5,
  output N_Flag,
  output Carry_Out
);

  wire n8bitalu_1_carry_out, n8bitalu_2_carry_out, n8bitalu_3_carry_out;

  _8BitALU u_8bitalu_1 (
    .out_9(out_5[7:0]), .F1(in_3[4]), .F0(in_3[5]), .ENB(in_3[2]), .B(in_2[7:0]), .ENA(in_3[3]),
    .A(in_1[7:0]), .INVA(in_3[1]), .in_8(in_3[0]), .Carry_Out(n8bitalu_1_carry_out));
  _8BitALU u_8bitalu_2 (
    .out_9(out_5[15:8]), .F1(in_3[4]), .F0(in_3[5]), .ENB(in_3[2]), .B(in_2[15:8]), .ENA(in_3[3]),
    .A(in_1[15:8]), .INVA(in_3[1]), .in_8(n8bitalu_1_carry_out), .Carry_Out(n8bitalu_2_carry_out));
  _8BitALU u_8bitalu_3 (
    .out_9(out_5[23:16]), .F1(in_3[4]), .F0(in_3[5]), .ENB(in_3[2]), .B(in_2[23:16]), .ENA(in_3[3]),
    .A(in_1[23:16]), .INVA(in_3[1]), .in_8(n8bitalu_2_carry_out), .Carry_Out(n8bitalu_3_carry_out));
  _8BitALU u_8bitalu_4 (
    .out_9({N_Flag, out_5[30:24]}), .F1(in_3[4]), .F0(in_3[5]), .ENB(in_3[2]), .B(in_2[31:24]),
    .ENA(in_3[3]), .A(in_1[31:24]), .INVA(in_3[1]), .in_8(n8bitalu_3_carry_out), .Carry_Out(Carry_Out));
  nor nor_1 (Z_Flag, out_5[0], out_5[1], out_5[2], out_5[3], out_5[4], out_5[5], out_5[6], out_5[7], out_5[8], out_5[9], out_5[10], out_5[11], out_5[12], out_5[13], out_5[14], out_5[15], out_5[16], out_5[17], out_5[18], out_5[19], out_5[20], out_5[21], out_5[22], out_5[23], out_5[24], out_5[25], out_5[26], out_5[27], out_5[28], out_5[29], out_5[30], N_Flag);

  assign out_5[31] = N_Flag;

  // Notes on the sheet:
  //   Carry In
  //   INVA
  //   A
  //   ENA
  //   B
  //   ENB
  //   F0
  //   F1
  //   Output
endmodule

// ALU
module ALU___Control (
  input  [7:0] in_1,
  output [1:0] out_2,
  output [5:0] out_3
);


  assign out_2 = in_1[7:6];
  assign out_3 = in_1[5:0];
endmodule

module B (
  input  [3:0] in_1,
  output [3:0] out_2
);


  assign out_2 = in_1;
endmodule

module C (
  input  [8:0] in_1,
  output out_2,
  output out_3,
  output out_4,
  output out_5,
  output out_6,
  output out_7,
  output out_8,
  output out_9,
  output out_10
);


  assign out_2 = in_1[8];
  assign out_3 = in_1[7];
  assign out_4 = in_1[6];
  assign out_5 = in_1[5];
  assign out_6 = in_1[4];
  assign out_7 = in_1[3];
  assign out_8 = in_1[2];
  assign out_9 = in_1[1];
  assign out_10 = in_1[0];
endmodule

module Control_Store (
  input  [8:0] in_1,
  output [31:0] out_2,
  output [3:0] out_3,
  output Halt
);

  wire not_2_out, not_3_out;
  wire [8:0] not_1_out;

  assign not_1_out = ~in_1;  // NOT_Gate not_1, 9 bits wide
  not not_2 (not_2_out, not_1_out[1]);
  not not_3 (not_3_out, not_1_out[3]);
  and and_1 (Halt, not_1_out[8], not_1_out[7], not_1_out[6], not_1_out[5], not_1_out[4], not_3_out, not_1_out[2], not_2_out, not_1_out[0]);
  ROM #(.addrWidth(9), .dataWidth(32)) rom_1 (.addr(in_1), .data(out_2));  // open: sel
  ROM #(.addrWidth(9), .dataWidth(4)) rom_2 (.addr(in_1), .data(out_3));  // open: sel

  // Notes on the sheet:
  //   in_1: pull=down
  //   contents of rom_1 (hex, n*v repeats v):
  //   20000000 27835220 14*3000000 20835048 3000000 3000000 71035021 3000000 11014800 10*3000000 70814008
  //   6083600c 1183c00a 21035048 1c03c008 1183c00a 73036048 6883c00a 1d814048 22835008 41814008 2383c00a
  //   1e035048 3000000 3000000 3000000 2003c214 2003f214 2000c214 2001c214 20014014 10814010 12014800
  //   20014214 38014014 2003c014 1403d014 16014014 26814014 3000000 3000000 3000000 435021 1b835021
  //   60035025 4883c021 25014021 15014023 60035021 72035021 1c835021 72835021 75835021 61835021 76035021
  //   40835021 3000000 48835021 7*3000000 4a03604a 3000000 1a035048 5*3000000 1003600a 7003604a 3000000
  //   3000000 3000000 7383604a 11*3000000 2303604a 4*3000000 3b03180a 3b839808 3c014042 3c839808 3d014102
  //   3d839808 3e014082 3e839808 14021 74036048 3000000 74835048 20014080 1481408a 1a014080 15814800
  //   11*3000000 400000 20000000 914000 93f000 60000000 41000000 a14000 3000000 3000000 6803600a 3000000
  //   6a03604a 3000000 3000000 3000000 1303604a 7*3000000 24836400 4*3000000 4a81404a 9*3000000 75035021
  //   9*3000000 20014200 20018200 49014200 6283f200 48035021 26035208 49814200 4b014200 8*3000000 61014400
  //   22035400 63014400 3000000 63814400 11*3000000 18014800 1a814804 7189c800 12814800 24014800 76894800
  //   69014802 18814800 19014800 19814800 77094800 77894800 78094800 2181c800 1381c800 2581c800 1d01c800
  //   16*3000000 24836400 19*3000000 91035021 12*3000000 91894800 a101c800 9c094800 17*3000000 92035021
  //   3000000 b801c800 9*3000000 1183c00a 44*3000000 1c03c008
  //   contents of rom_2 (hex, n*v repeats v):
  //   0 1 14*0 4 0 0 1 0 5 10*0 4 4 3 4 3 6 4 6 0 5 4 3 4 7*0 7 7 5 2 7 2 4 8 5 0 0 0 1 1 1 8 0 0 8*1 0 1
  //   7*0 4 0 4 5*0 4 4 0 0 0 4 11*0 4 13*0 4 0 4 7 0 0 5 13*0 8 8 0 0 8 0 0 4 0 4 0 0 0 4 7*0 1 4*0 5 9*0
  //   1 12*0 4 1 7 10*0 7 1 7 0 7 11*0 7 0 3 3 0 2 0 7 7 7 7*3 16*0 1 19*0 1 12*0 3 3 3 17*0 1 0 3 9*0 5
  //   44*0 5
endmodule

module CPP (
  input  [31:0] in_1,
  input  Enabled,
  input  Clock,
  input  Enable_Output,
  output [31:0] Probe,
  output [31:0] out_6
);

  wire [31:0] bit_extender_1_out;

  Register #(.width(32)) register_1 (.D(in_1), .en(Enabled), .Q(Probe), .clk(Clock));  // open: clr
  assign bit_extender_1_out = {{31{Enable_Output}}, Enable_Output};  // Bit_Extender bit_extender_1
  assign out_6 = Probe & bit_extender_1_out;  // AND_Gate and_1, 32 bits wide

  // Notes on the sheet:
  //   and_1 drives only 1 and floats otherwise
  //   Output
endmodule

module Decoder (
  input  [3:0] in_1,
  output out_2,
  output out_3,
  output out_4,
  output out_5,
  output out_6,
  output out_7,
  output out_8,
  output out_9,
  output out_10
);

  Decoder_part #(.select(4)) decoder_1 (
    .out0(out_2), .out1(out_3), .out2(out_4), .out3(out_5), .out4(out_6), .out5(out_7), .out6(out_8),
    .out7(out_9), .out8(out_10), .sel(in_1));  // open: out9, out10, out11, out12, out13, out14, out15, en
endmodule

module H (
  input  [31:0] C_Bus,
  input  Enable_C_Bus,
  input  Clock,
  output [31:0] A_Bus,
  output [31:0] Probe
);

  Register #(.width(32)) register_1 (.D(C_Bus), .en(Enable_C_Bus), .Q(A_Bus), .clk(Clock));  // open: clr

  assign Probe = A_Bus;
endmodule

module High_Bit (
  input  N,
  input  in_2,
  input  [1:0] JAMN_JAMZ,
  input  Z,
  output out_5
);

  wire and_1_out, and_2_out;

  D_Flip_Flop d_ff_1 (.clk(in_2), .D(N));  // open: Q, Qn, preset, en, reset
  D_Flip_Flop d_ff_2 (.clk(in_2), .D(Z));  // open: Q, Qn, preset, en, reset
  and and_1 (and_1_out, N, JAMN_JAMZ[1]);
  and and_2 (and_2_out, JAMN_JAMZ[0], Z);
  or or_1 (out_5, and_1_out, and_2_out);
endmodule

module J (
  input  [2:0] in_1,
  output out_2,
  output [1:0] out_3
);


  assign out_2 = in_1[2];
  assign out_3 = in_1[1:0];

  // Notes on the sheet:
  //   in_1: pull=down
endmodule

module LV (
  input  [31:0] C_Bus,
  input  C_Bus_Enabled,
  input  Clock,
  input  Enable_B_Bus,
  output [31:0] Probe,
  output [31:0] B_Bus
);

  wire [31:0] bit_extender_1_out;

  Register #(.width(32)) register_1 (.D(C_Bus), .en(C_Bus_Enabled), .Q(Probe), .clk(Clock));  // open: clr
  assign bit_extender_1_out = {{31{Enable_B_Bus}}, Enable_B_Bus};  // Bit_Extender bit_extender_1
  assign B_Bus = Probe & bit_extender_1_out;  // AND_Gate and_1, 32 bits wide

  // Notes on the sheet:
  //   and_1 drives only 1 and floats otherwise
endmodule

module M (
  input  [2:0] in_1,
  output [2:0] out_2
);


  assign out_2 = in_1;
endmodule

module MAR (
  input  [31:0] Input_from_C_Bus,
  input  Clock,
  input  Enable_C_Bus,
  output [31:0] Probe_Output,
  output [31:0] Output_to_RAM
);

  Register #(.width(32)) register_1 (
    .D(Input_from_C_Bus), .en(Enable_C_Bus), .Q(Output_to_RAM), .clk(Clock));  // open: clr

  assign Probe_Output = Output_to_RAM;
endmodule

module MBR (
  input  [7:0] RAM_Input,
  input  Clock,
  input  [2:0] WRF,
  input  Signed_Output,
  input  Unsigned_Output,
  output [7:0] Probe_Output,
  output [7:0] To_Juntion_Box,
  output [31:0] Signed_Output_2,
  output [31:0] Unsigned_Output_2
);

  wire and_1_out, d_ff_1_q, wrf_splitter_1_fetch;
  wire [31:0] bit_extender_1_out, bit_extender_2_out, bit_extender_3_out, bit_extender_4_out;

  WRF_Splitter wrf_splitter_1 (.WRF(WRF), .Fetch(wrf_splitter_1_fetch));  // open: Read, Write
  and and_1 (and_1_out, Clock, wrf_splitter_1_fetch);
  D_Flip_Flop #(.trigger("high")) d_ff_1 (.clk(Clock), .D(and_1_out), .Q(d_ff_1_q));  // open: Qn, preset, en, reset
  Register register_1 (.D(RAM_Input), .en(d_ff_1_q), .Q(Probe_Output), .clk(Clock));  // open: clr
  assign bit_extender_1_out = {{31{Signed_Output}}, Signed_Output};  // Bit_Extender bit_extender_1
  assign bit_extender_2_out = {{24{Probe_Output[7]}}, Probe_Output};  // Bit_Extender bit_extender_2
  assign bit_extender_3_out = {{24{1'b0}}, Probe_Output};  // Bit_Extender bit_extender_3
  assign bit_extender_4_out = {{31{Unsigned_Output}}, Unsigned_Output};  // Bit_Extender bit_extender_4
  assign Signed_Output_2 = bit_extender_1_out & bit_extender_2_out;  // AND_Gate and_2, 32 bits wide
  assign Unsigned_Output_2 = bit_extender_3_out & bit_extender_4_out;  // AND_Gate and_3, 32 bits wide

  assign To_Juntion_Box = Probe_Output;

  // Notes on the sheet:
  //   and_2 drives only 1 and floats otherwise
  //   and_3 drives only 1 and floats otherwise
endmodule

module MDR (
  input  [2:0] WRF,
  input  [31:0] Input_from_RAM,
  input  C_Bus_Enabled,
  input  Clock,
  input  [31:0] C_Bus_Input,
  input  Enable_B_Bus,
  output [31:0] Output_to_RAM,
  output [31:0] Probe_Output,
  output [31:0] B_Bus_Output
);

  wire and_1_out, d_ff_1_q, or_1_out, read, write;
  wire [31:0] and_2_out, and_3_out, bit_extender_1_out, bit_extender_2_out, bit_extender_3_out,
       bit_extender_4_out, or_2_out;

  and and_1 (and_1_out, Clock, read);
  D_Flip_Flop #(.trigger("high")) d_ff_1 (.clk(Clock), .D(and_1_out), .Q(d_ff_1_q));  // open: Qn, preset, en, reset
  WRF_Splitter wrf_splitter_1 (.WRF(WRF), .Read(read), .Write(write));  // open: Fetch
  assign and_2_out = Input_from_RAM & bit_extender_1_out;  // AND_Gate and_2, 32 bits wide
  assign bit_extender_1_out = {{31{d_ff_1_q}}, d_ff_1_q};  // Bit_Extender bit_extender_1
  or or_1 (or_1_out, d_ff_1_q, C_Bus_Enabled);
  assign bit_extender_2_out = {{31{C_Bus_Enabled}}, C_Bus_Enabled};  // Bit_Extender bit_extender_2
  assign and_3_out = bit_extender_2_out & C_Bus_Input;  // AND_Gate and_3, 32 bits wide
  assign or_2_out = and_2_out | and_3_out;  // OR_Gate or_2, 32 bits wide
  assign bit_extender_3_out = {{31{write}}, write};  // Bit_Extender bit_extender_3
  Register #(.width(32)) register_1 (.D(or_2_out), .en(or_1_out), .Q(Probe_Output), .clk(Clock));  // open: clr
  assign bit_extender_4_out = {{31{Enable_B_Bus}}, Enable_B_Bus};  // Bit_Extender bit_extender_4
  assign Output_to_RAM = bit_extender_3_out & Probe_Output;  // AND_Gate and_4, 32 bits wide
  assign B_Bus_Output = Probe_Output & bit_extender_4_out;  // AND_Gate and_5, 32 bits wide

  // Notes on the sheet:
  //   and_5 drives only 1 and floats otherwise
endmodule

module MI_Display (
  input  [8:0] Microinstruction,
  output [3:0] out_2,
  output [3:0] out_3,
  output [3:0] out_4,
  output out_5,
  output out_6,
  output out_7
);


  assign out_2 = {3'b000, Microinstruction[8]};
  assign out_3 = Microinstruction[7:4];
  assign out_4 = Microinstruction[3:0];
  assign out_5 = 1'b0;
  assign out_6 = 1'b0;
  assign out_7 = 1'b0;
endmodule

module MIR (
  input  [31:0] in_1,
  output out_2,
  output [2:0] out_3,
  output [8:0] out_4,
  output [1:0] out_5,
  output [1:0] out_6,
  output [5:0] out_7,
  output out_8,
  output out_9,
  output out_10,
  output out_11,
  output out_12,
  output out_13,
  output out_14,
  output out_15,
  output out_16
);

  Addr addr_1 (.in_1(in_1[31:23]), .out_2(out_4));
  J j_1 (.in_1(in_1[22:20]), .out_3(out_5), .out_2(out_2));
  ALU___Control alu_control_1 (.in_1(in_1[19:12]), .out_2(out_6), .out_3(out_7));
  C c_1 (
    .in_1(in_1[11:3]), .out_2(out_8), .out_3(out_9), .out_4(out_10), .out_5(out_11), .out_6(out_12),
    .out_7(out_13), .out_8(out_14), .out_9(out_15), .out_10(out_16));
  M m_1 (.in_1(in_1[2:0]), .out_2(out_3));
endmodule

module MPC (
  input  [8:0] in_1,
  input  in_2,
  input  in_3,
  output [8:0] out_4
);

  wire [8:0] or_1_out;

  assign or_1_out = in_1 | {in_2, {8{1'b0}}};  // OR_Gate or_1, 9 bits wide
  Register #(.width(9)) register_1 (.D(or_1_out), .Q(out_4), .clk(in_3));  // open: en, clr
endmodule

module O (
  input  [8:0] ADDR,
  input  [7:0] MBR,
  input  JMPC,
  output [8:0] out_4
);

  wire [8:0] and_1_out, and_2_out, bit_extender_1_out, bit_extender_2_out, not_1_out, or_1_out;

  assign bit_extender_1_out = {{1{1'b0}}, MBR};  // Bit_Extender bit_extender_1
  assign bit_extender_2_out = {{8{JMPC}}, JMPC};  // Bit_Extender bit_extender_2
  assign or_1_out = ADDR | bit_extender_1_out;  // OR_Gate or_1, 9 bits wide
  assign not_1_out = ~bit_extender_2_out;  // NOT_Gate not_1, 9 bits wide
  assign and_1_out = ADDR & not_1_out;  // AND_Gate and_1, 9 bits wide
  assign and_2_out = or_1_out & bit_extender_2_out;  // AND_Gate and_2, 9 bits wide
  assign out_4 = and_1_out | and_2_out;  // OR_Gate or_2, 9 bits wide
endmodule

module OPC (
  input  [31:0] in_1,
  input  Enabled,
  input  Clock,
  input  Enable_Output,
  output [31:0] Probe,
  output [31:0] out_6
);

  wire [31:0] bit_extender_1_out;

  Register #(.width(32)) register_1 (.D(in_1), .en(Enabled), .Q(Probe), .clk(Clock));  // open: clr
  assign bit_extender_1_out = {{31{Enable_Output}}, Enable_Output};  // Bit_Extender bit_extender_1
  assign out_6 = Probe & bit_extender_1_out;  // AND_Gate and_1, 32 bits wide

  // Notes on the sheet:
  //   and_1 drives only 1 and floats otherwise
  //   Output
endmodule

module PC (
  input  [31:0] C_Bus_Input,
  input  Enable_C_Bus,
  input  Clock,
  input  Enable_B_Bus,
  output [31:0] RAM_Output,
  output [31:0] Probe_Output,
  output [31:0] B_Bus_Output
);

  wire [31:0] bit_extender_1_out;

  Register #(.width(32)) register_1 (.D(C_Bus_Input), .en(Enable_C_Bus), .Q(Probe_Output), .clk(Clock));  // open: clr
  assign bit_extender_1_out = {{31{Enable_B_Bus}}, Enable_B_Bus};  // Bit_Extender bit_extender_1
  assign B_Bus_Output = Probe_Output & bit_extender_1_out;  // AND_Gate and_1, 32 bits wide

  assign RAM_Output = Probe_Output;

  // Notes on the sheet:
  //   and_1 drives only 1 and floats otherwise
endmodule

module RAM (
  input  rw_clock,
  input  f_clock,
  input  [2:0] WRF,
  input  [31:0] MAR,
  input  [31:0] MDR,
  input  [31:0] PC,
  output [31:0] MDR_2,
  output [7:0] MBR
);

  wire and_1_out, and_2_out, buffer_1_out, buffer_2_out, buffer_3_out, buffer_4_out, buffer_5_out, fetch,
       nand_1_out, nand_2_out, or_1_out, or_2_out, read, write;
  wire [1:0] ctr;
  wire [7:0] multiplexer_1_out;
  wire [23:0] and_3_out, and_4_out, bit_extender_2_out, bit_extender_3_out, bit_extender_4_out, or_3_out;
  wire [23:2] bit_extender_1_out;
  wire [31:0] buffer_6_out, ram_1_data;

  or or_1 (or_1_out, read, write);
  nand nand_1 (nand_1_out, rw_clock, f_clock);
  Bit_Extender #(.in_width(32), .out_width(24), .\type ("sign")) bit_extender_1 (
    .in(PC), .out({bit_extender_1_out, ctr}));
  Bit_Extender #(.in_width(32), .out_width(24), .\type ("sign")) bit_extender_2 (.in(MAR), .out(bit_extender_2_out));
  and and_1 (and_1_out, or_1_out, nand_1_out, rw_clock);
  assign bit_extender_3_out = {{23{and_1_out}}, and_1_out};  // Bit_Extender bit_extender_3
  and and_2 (and_2_out, f_clock, nand_1_out, fetch);
  assign bit_extender_4_out = {{23{and_2_out}}, and_2_out};  // Bit_Extender bit_extender_4
  assign and_3_out = bit_extender_2_out & bit_extender_3_out;  // AND_Gate and_3, 24 bits wide
  or or_2 (or_2_out, rw_clock, f_clock);
  assign and_4_out = bit_extender_4_out & {2'b00, bit_extender_1_out};  // AND_Gate and_4, 24 bits wide
  assign or_3_out = and_3_out | and_4_out;  // OR_Gate or_3, 24 bits wide
  buf buffer_1 (buffer_1_out, buffer_4_out);
  buf buffer_2 (buffer_2_out, buffer_1_out);
  buf buffer_3 (buffer_3_out, buffer_2_out);
  buf buffer_4 (buffer_4_out, or_2_out);
  buf buffer_5 (buffer_5_out, buffer_3_out);
  WRF_Splitter wrf_splitter_1 (.WRF(WRF), .Fetch(fetch), .Read(read), .Write(write));
  RAM_part #(.addrWidth(24), .dataWidth(32), .bus("separate")) ram_1 (
    .addr(or_3_out), .din(MDR), .data(ram_1_data), .str(write), .clk(buffer_5_out), .ld(nand_2_out));  // open: sel, clr
  nand nand_2 (nand_2_out, rw_clock, write);
  assign buffer_6_out = ram_1_data;  // Buffer buffer_6, 32 bits wide
  Multiplexer #(.select(2), .width(8)) multiplexer_1 (
    .in0(buffer_6_out[31:24]), .in1(buffer_6_out[23:16]), .in2(buffer_6_out[15:8]), .in3(buffer_6_out[7:0]),
    .out(multiplexer_1_out), .sel(ctr));  // open: en
  // Probe on multiplexer_1_out
  Register #(.width(32), .trigger("high")) register_1 (
    .D(buffer_6_out), .en(read), .Q(MDR_2), .clk(rw_clock));  // open: clr
  Register #(.trigger("falling")) register_2 (.D(multiplexer_1_out), .en(fetch), .Q(MBR), .clk(f_clock));  // open: clr
endmodule

module Shifter (
  input  [31:0] in_1,
  input  [1:0] Controls,
  output [31:0] out_3
);

  wire [31:0] demultiplexer_1_out0, demultiplexer_1_out1, demultiplexer_1_out2, demultiplexer_1_out3,
       shifter_1_out, shifter_2_out, undriven;

  Demultiplexer #(.select(2), .width(32)) demultiplexer_1 (
    .out0(demultiplexer_1_out0), .out1(demultiplexer_1_out1), .out2(demultiplexer_1_out2),
    .out3(demultiplexer_1_out3), .in(in_1), .sel(Controls));  // open: en
  Shifter_part #(.width(32), .shift("ar")) shifter_1 (
    .in(demultiplexer_1_out1), .\dist (5'b00001), .out(shifter_1_out));
  Shifter_part #(.width(32)) shifter_2 (.in(demultiplexer_1_out2), .\dist (5'b01000), .out(shifter_2_out));
  Multiplexer #(.select(2), .width(32)) multiplexer_1 (
    .in0(demultiplexer_1_out0), .in1(shifter_1_out), .in2(shifter_2_out), .in3(undriven), .out(out_3),
    .sel(Controls));  // open: en

  // Notes on the sheet:
  //   Input
  //   Shifter
  //   Output
endmodule

module SP (
  input  [31:0] C_Bus,
  input  Enable_C_Bus,
  input  Clock,
  input  Enable_B_Bus,
  output [31:0] Probe,
  output [31:0] B_Bus
);

  wire [31:0] bit_extender_1_out;

  Register #(.width(32)) register_1 (.D(C_Bus), .en(Enable_C_Bus), .Q(Probe), .clk(Clock));  // open: clr
  assign bit_extender_1_out = {{31{Enable_B_Bus}}, Enable_B_Bus};  // Bit_Extender bit_extender_1
  assign B_Bus = Probe & bit_extender_1_out;  // AND_Gate and_1, 32 bits wide

  // Notes on the sheet:
  //   and_1 drives only 1 and floats otherwise
endmodule

module TOS (
  input  [31:0] in_1,
  input  Enabled,
  input  Clock,
  input  Enable_Output,
  output [31:0] Probe,
  output [31:0] out_6
);

  wire [31:0] bit_extender_1_out;

  Register #(.width(32)) register_1 (.D(in_1), .en(Enabled), .Q(Probe), .clk(Clock));  // open: clr
  assign bit_extender_1_out = {{31{Enable_Output}}, Enable_Output};  // Bit_Extender bit_extender_1
  assign out_6 = Probe & bit_extender_1_out;  // AND_Gate and_1, 32 bits wide

  // Notes on the sheet:
  //   and_1 drives only 1 and floats otherwise
  //   Output
endmodule

module Wired_Machine (
);

  MAR mar_1 ();  // open: Input_from_C_Bus, Clock, Enable_C_Bus, Output_to_RAM, Probe_Output
  MBR mbr_1 ();  // open: RAM_Input, Signed_Output, Signed_Output_2, Unsigned_Output_2, Unsigned_Output, To_Juntion_Box, Probe_Output, WRF, Clock
  SP sp_1 ();  // open: C_Bus, Clock, Enable_C_Bus, B_Bus, Enable_B_Bus, Probe
  LV lv_1 ();  // open: C_Bus, Clock, C_Bus_Enabled, B_Bus, Enable_B_Bus, Probe
  CPP cpp_1 ();  // open: in_1, Clock, Enabled, out_6, Enable_Output, Probe
  TOS tos_1 ();  // open: in_1, Clock, Enabled, out_6, Enable_Output, Probe
  OPC opc_1 ();  // open: in_1, Clock, Enabled, out_6, Enable_Output, Probe
  H h_1 ();  // open: C_Bus, Clock, Enable_C_Bus, A_Bus, Probe
  ALU alu_1 ();  // open: Z_Flag, in_1, in_2, out_5, in_3, N_Flag, Carry_Out
  MDR mdr_1 ();  // open: C_Bus_Input, Clock, C_Bus_Enabled, B_Bus_Output, Enable_B_Bus, Input_from_RAM, Output_to_RAM, WRF, Probe_Output
  PC pc_1 ();  // open: C_Bus_Input, Clock, B_Bus_Output, Enable_B_Bus, Enable_C_Bus, RAM_Output, Probe_Output
  Shifter shifter_1 ();  // open: in_1, out_3, Controls
  Decoder decoder_1 ();  // open: in_1, out_2, out_3, out_4, out_5, out_6, out_7, out_8, out_9, out_10
  High_Bit high_bit_1 ();  // open: N, out_5, in_2, JAMN_JAMZ, Z
  MPC mpc_1 ();  // open: out_4, in_2, in_1, in_3
  O o_1 ();  // open: ADDR, out_4, MBR, JMPC
  Addr addr_1 ();  // open: in_1, out_2
  J j_1 ();  // open: in_1, out_3, out_2
  ALU___Control alu_control_1 ();  // open: in_1, out_2, out_3
  Control_Store control_store_1 ();  // open: out_2, out_3, in_1, Halt
  C c_1 ();  // open: in_1, out_2, out_3, out_4, out_5, out_6, out_7, out_8, out_9, out_10
  M m_1 ();  // open: in_1, out_2
  B b_1 ();  // open: in_1, out_2
endmodule

module _1BitAdder (
  input  Carry_In,
  input  A,
  input  B,
  input  Function,
  output Result,
  output Carry_Out
);

  wire and_1_out, and_2_out, xor_1_out, xor_2_out;

  and and_1 (and_1_out, Function, B, A);
  or or_1 (Carry_Out, and_1_out, and_2_out);
  xor xor_1 (xor_1_out, A, B);
  and and_2 (and_2_out, Function, xor_1_out, Carry_In);
  xor xor_2 (xor_2_out, Carry_In, xor_1_out);
  and and_3 (Result, xor_2_out, Function);
endmodule

module _1BitALU (
  input  Carry_In,
  input  A,
  input  ENA,
  input  B,
  input  ENB,
  input  in_6,
  input  F1,
  input  F0,
  output Output,
  output out_10
);

  wire and_1_out, and_2_out, and_3_out, and_4_out, and_5_out, and_6_out, decoder_1_out0, decoder_1_out1,
       decoder_1_out2, decoder_1_out3, n1bitadder_1_result, not_1_out, or_1_out, xor_1_out;

  and and_1 (and_1_out, ENA, B);
  and and_2 (and_2_out, ENB, in_6);
  xor xor_1 (xor_1_out, A, and_1_out);
  not not_1 (not_1_out, and_2_out);
  Decoder_part #(.select(2)) decoder_1 (
    .out0(decoder_1_out0), .out1(decoder_1_out1), .out2(decoder_1_out2), .out3(decoder_1_out3), .sel({F0, F1}));  // open: en
  and and_3 (and_3_out, xor_1_out, and_2_out);
  or or_1 (or_1_out, xor_1_out, and_2_out);
  and and_4 (and_4_out, and_3_out, decoder_1_out0);
  and and_5 (and_5_out, or_1_out, decoder_1_out1);
  and and_6 (and_6_out, not_1_out, decoder_1_out2);
  _1BitAdder u_1bitadder_1 (
    .A(and_2_out), .B(xor_1_out), .Function(decoder_1_out3), .Result(n1bitadder_1_result),
    .Carry_In(Carry_In), .Carry_Out(out_10));
  or or_2 (Output, and_4_out, and_5_out, and_6_out, n1bitadder_1_result);

  // Notes on the sheet:
  //   INVA
endmodule

module _8BitALU (
  input  F1,
  input  F0,
  input  ENB,
  input  [7:0] B,
  input  ENA,
  input  [7:0] A,
  input  INVA,
  input  in_8,
  output [7:0] out_9,
  output Carry_Out
);

  wire n1bitalu_2_out_10, n1bitalu_3_out_10, n1bitalu_4_out_10, n1bitalu_5_out_10, n1bitalu_6_out_10,
       n1bitalu_7_out_10, n1bitalu_8_out_10;

  _1BitALU u_1bitalu_1 (
    .Carry_In(n1bitalu_2_out_10), .A(INVA), .ENA(A[7]), .B(ENA), .ENB(B[7]), .in_6(ENB), .F1(F1), .F0(F0),
    .Output(out_9[7]), .out_10(Carry_Out));
  _1BitALU u_1bitalu_2 (
    .Carry_In(n1bitalu_3_out_10), .A(INVA), .ENA(A[6]), .B(ENA), .ENB(B[6]), .in_6(ENB), .F1(F1), .F0(F0),
    .Output(out_9[6]), .out_10(n1bitalu_2_out_10));
  _1BitALU u_1bitalu_3 (
    .Carry_In(n1bitalu_4_out_10), .A(INVA), .ENA(A[5]), .B(ENA), .ENB(B[5]), .in_6(ENB), .F1(F1), .F0(F0),
    .Output(out_9[5]), .out_10(n1bitalu_3_out_10));
  _1BitALU u_1bitalu_4 (
    .Carry_In(n1bitalu_5_out_10), .A(INVA), .ENA(A[4]), .B(ENA), .ENB(B[4]), .in_6(ENB), .F1(F1), .F0(F0),
    .Output(out_9[4]), .out_10(n1bitalu_4_out_10));
  _1BitALU u_1bitalu_5 (
    .Carry_In(n1bitalu_6_out_10), .A(INVA), .ENA(A[3]), .B(ENA), .ENB(B[3]), .in_6(ENB), .F1(F1), .F0(F0),
    .Output(out_9[3]), .out_10(n1bitalu_5_out_10));
  _1BitALU u_1bitalu_6 (
    .Carry_In(n1bitalu_7_out_10), .A(INVA), .ENA(A[2]), .B(ENA), .ENB(B[2]), .in_6(ENB), .F1(F1), .F0(F0),
    .Output(out_9[2]), .out_10(n1bitalu_6_out_10));
  _1BitALU u_1bitalu_7 (
    .Carry_In(n1bitalu_8_out_10), .A(INVA), .ENA(A[1]), .B(ENA), .ENB(B[1]), .in_6(ENB), .F1(F1), .F0(F0),
    .Output(out_9[1]), .out_10(n1bitalu_7_out_10));
  _1BitALU u_1bitalu_8 (
    .Carry_In(in_8), .A(INVA), .ENA(A[0]), .B(ENA), .ENB(B[0]), .in_6(ENB), .F1(F1), .F0(F0),
    .Output(out_9[0]), .out_10(n1bitalu_8_out_10));

  // Notes on the sheet:
  //   Out
  //   Carry In
endmodule

module _32BitALU (
  input  [31:0] in_1,
  input  [31:0] in_2,
  input  [5:0] in_3,
  output Z_Flag,
  output [31:0] out_5,
  output N_Flag,
  output Carry_Out
);

  wire n8bitalu_1_p9, n8bitalu_2_p10, n8bitalu_3_p10;

  // _8BitALU 8bitalu_1: pin names not known; wires that end beside it: in_3[1], in_1[7:0], in_3[3], in_2[7:0], in_3[2], in_3[5], in_3[4], in_3[0], n8bitalu_1_p9, out_5[7:0], out_5[15:8]
  // _8BitALU 8bitalu_2: pin names not known; wires that end beside it: in_3[1], in_1[15:8], in_3[3], in_2[15:8], in_3[2], in_3[5], in_3[4], n8bitalu_1_p9, n8bitalu_1_p9, n8bitalu_2_p10, out_5[15:8]
  // _8BitALU 8bitalu_3: pin names not known; wires that end beside it: in_3[1], in_1[23:16], in_3[3], in_2[23:16], in_3[2], in_3[5], in_3[4], n8bitalu_2_p10, n8bitalu_2_p10, n8bitalu_3_p10, out_5[23:16]
  // _8BitALU 8bitalu_4: pin names not known; wires that end beside it: in_3[1], in_1[31:24], in_3[3], in_2[31:24], in_3[2], in_3[5], in_3[4], n8bitalu_3_p10, n8bitalu_3_p10, Carry_Out, {N_Flag, out_5[30:24]}
  nor nor_1 (Z_Flag, out_5[0], out_5[1], out_5[2], out_5[3], out_5[4], out_5[5], out_5[6], out_5[7], out_5[8], out_5[9], out_5[10], out_5[11], out_5[12], out_5[13], out_5[14], out_5[15], out_5[16], out_5[17], out_5[18], out_5[19], out_5[20], out_5[21], out_5[22], out_5[23], out_5[24], out_5[25], out_5[26], out_5[27], out_5[28], out_5[29], out_5[30], N_Flag);

  assign out_5[31] = N_Flag;

  // Notes on the sheet:
  //   Carry In
  //   INVA
  //   A
  //   ENA
  //   B
  //   ENB
  //   F0
  //   F1
  //   Output
endmodule

module WRF_Splitter (
  input  [2:0] WRF,
  output Fetch,
  output Read,
  output Write
);


  assign Fetch = WRF[0];
  assign Read = WRF[1];
  assign Write = WRF[2];
endmodule

module Master_Clock (
  input  Halt,
  output Out_0,
  output Out_1,
  output Out_2,
  output Out_3
);

  wire not_1_out;
  wire [1:0] clock_1_out, controlled_buffer_1_out;

  not not_1 (not_1_out, Halt);
  Clock clock_1 (.out(clock_1_out[0]));
  Decoder_part #(.select(2)) decoder_1 (
    .out0(Out_0), .out1(Out_1), .out2(Out_2), .out3(Out_3), .sel(controlled_buffer_1_out));  // open: en
  assign controlled_buffer_1_out = not_1_out ? clock_1_out : 2'bz;  // Controlled_Buffer controlled_buffer_1
  Clock #(.highDuration(2), .lowDuration(2)) clock_2 (.out(clock_1_out[1]));
endmodule
