// Logisim project Junction-Box.circ as structural Verilog: 2 circuits, main circuit main
module main (
  input  [7:0] ADDR,
  input  [7:0] MBR,
  input  JMPC,
  output [7:0] out_4
);

  wire [7:0] and_1_out, and_2_out, bit_extender_1_out, not_1_out, or_1_out;

  assign bit_extender_1_out = {{7{JMPC}}, JMPC};  // Bit_Extender bit_extender_1
  assign or_1_out = ADDR | MBR;  // OR_Gate or_1, 8 bits wide
  assign not_1_out = ~bit_extender_1_out;  // NOT_Gate not_1, 8 bits wide
  assign and_1_out = ADDR & not_1_out;  // AND_Gate and_1, 8 bits wide
  assign and_2_out = or_1_out & bit_extender_1_out;  // AND_Gate and_2, 8 bits wide
  assign out_4 = and_1_out | and_2_out;  // OR_Gate or_2, 8 bits wide
endmodule

module Junction_Box (
  input  [7:0] ADDR,
  input  [7:0] MBR,
  input  JMPC,
  output [7:0] out_4
);

  wire [7:0] and_1_out, and_2_out, bit_extender_1_out, not_1_out, or_1_out;

  assign bit_extender_1_out = {{7{JMPC}}, JMPC};  // Bit_Extender bit_extender_1
  assign or_1_out = ADDR | MBR;  // OR_Gate or_1, 8 bits wide
  assign not_1_out = ~bit_extender_1_out;  // NOT_Gate not_1, 8 bits wide
  assign and_1_out = ADDR & not_1_out;  // AND_Gate and_1, 8 bits wide
  assign and_2_out = or_1_out & bit_extender_1_out;  // AND_Gate and_2, 8 bits wide
  assign out_4 = and_1_out | and_2_out;  // OR_Gate or_2, 8 bits wide
endmodule
