// Logisim project RAM.circ as structural Verilog
module ByteAddressableRAM (
  input  [23:0] in_1,
  input  Type,
  input  [31:0] in_3,
  input  Clear,
  input  in_5,
  output [31:0] out_6,
  output [7:0] MBR,
  output [7:0] out_8
);

  wire decoder_1_out0, decoder_1_out1, decoder_1_out2, decoder_1_out3, not_1_out;
  wire [1:0] clock_1_out;
  wire [7:0] ram_1_data;
  wire [23:0] controlled_buffer_1_out;

  Clock clock_1 (.out(clock_1_out[0]));
  Clock #(.highDuration(2), .lowDuration(2)) clock_2 (.out(clock_1_out[1]));
  not not_1 (not_1_out, Type);
  Multiplexer #(.select(2), .width(8)) multiplexer_1 (
    .in0(in_3[7:0]), .in1(in_3[15:8]), .in2(in_3[23:16]), .in3(in_3[31:24]), .out(out_8), .sel(clock_1_out));  // open: en
  assign controlled_buffer_1_out = not_1_out ? in_1 : 24'bz;  // Controlled_Buffer controlled_buffer_1
  assign controlled_buffer_1_out = Type ? {in_1[21:0], clock_1_out} : 24'bz;  // Controlled_Buffer controlled_buffer_2
  RAM #(.addrWidth(24), .bus("separate")) ram_1 (
    .addr(controlled_buffer_1_out), .din(out_8), .data(ram_1_data), .clk(in_5));  // open: str, sel, ld, clr
  Decoder #(.select(2)) decoder_1 (
    .out0(decoder_1_out0), .out1(decoder_1_out1), .out2(decoder_1_out2), .out3(decoder_1_out3),
    .sel(clock_1_out));  // open: en
  Register #(.trigger("falling")) register_1 (.D(ram_1_data), .Q(MBR), .clk(decoder_1_out0), .clr(Clear));  // open: en
  Register #(.trigger("falling")) register_2 (
    .D(ram_1_data), .Q(out_6[15:8]), .clk(decoder_1_out1), .clr(Clear));  // open: en
  Register #(.trigger("falling")) register_3 (
    .D(ram_1_data), .Q(out_6[23:16]), .clk(decoder_1_out2), .clr(Clear));  // open: en
  Register #(.trigger("falling")) register_4 (
    .D(ram_1_data), .Q(out_6[31:24]), .clk(decoder_1_out3), .clr(Clear));  // open: en

  assign out_6[7:0] = MBR;

  // Notes on the sheet:
  //   0 = byte address
  //   1 = word address
  //   Address
  //   MDR
endmodule

module WordAddressableRAM (
  input  [23:0] in_1,
  input  Type,
  output [31:0] out_3,
  output [7:0] MBR
);

  wire not_1_out;
  wire [23:0] controlled_buffer_1_out;

  assign controlled_buffer_1_out = Type ? in_1 : 24'bz;  // Controlled_Buffer controlled_buffer_1
  not not_1 (not_1_out, Type);
  assign controlled_buffer_1_out = not_1_out ? {2'b00, in_1[23:2]} : 24'bz;  // Controlled_Buffer controlled_buffer_2
  RAM #(.addrWidth(24), .dataWidth(32)) ram_1 (
    .addr(controlled_buffer_1_out), .data(out_3));  // open: sel, clk, ld, clr
  Multiplexer #(.select(2), .width(8)) multiplexer_1 (
    .in0(out_3[31:24]), .in1(out_3[23:16]), .in2(out_3[15:8]), .in3(out_3[7:0]), .out(MBR), .sel(in_1[1:0]));  // open: en

  // Notes on the sheet:
  //   0 = byte addressable
  //   1 = word addressable
  //   Address
  //   MDR
endmodule
